# Fritzing sketch cardreader-interface (saved by Fritzing 0.9.0b)
breadboards: 1

parts:
  R1 = Resistor [tolerance=±5% resistance=1k package=THT]
  Pi_Vcc = female pin header, 1 pin [form="♀ (female)"]
  Pi_gpio_input = female pin header, 1 pin [form="♀ (female)"]
  U1 = PS2502 [part_number=PS2502 package=cnz1120]
  Card_reader_dataline = female pin header, 1 pin [form="♀ (female)"]

nets:
  GND: R1.Pin_0, U1.2
  N1: R1.Pin_1, Pi_gpio_input.pin1, U1.4
  N2: Pi_Vcc.pin1, U1.3
  N3: U1.1, Card_reader_dataline.pin1

custom parts:
  PS2502: LED-to-NPN high current optoisolator
