# Fritzing sketch loop-sense-isolated (saved by Fritzing 0.9.0b)
breadboards: 1

parts:
  R1 = Resistor [tolerance=±5% resistance=4.7k package=THT]
  U1 = PS2502 [part_number=PS2502 package=cnz1120]
  +12v = single row smd female pin header, 1 pin [form="♀ (female)"]
  Pi_gpio_input_w/internal_pullup_active = female pin header, 1 pin [form="♀ (female)"]
  Magnetic_Switch = Pushbutton [package=THT]

nets:
  N1: R1.Pin_0, Magnetic_Switch.leg1
  N2: R1.Pin_1, U1.1
  GND: U1.2, U1.4
  N3: U1.3, Pi_gpio_input_w/internal_pullup_active.pin1
  N4: +12v.pin1, Magnetic_Switch.leg0

notes:
  The magnetic loop switch may be hundreds of feet away from R1. The loop switch is mounted on a door. The gpio goes low when the door is closed.

custom parts:
  PS2502: LED-to-NPN high current optoisolator
