# Fritzing sketch solenoid-control-schematic (saved by Fritzing 0.9.0b)
breadboards: 1

parts:
  U1 = PS2502 [part_number=PS2502 package=cnz1120]
  12_volt_relay = RELAY [package=relay-jzc]
  R1 = Resistor [tolerance=±5% resistance=2.2k package="0603 [SMD]"]
  Pi_door_control_gpio = female pin header, 1 pin [form="♀ (female)"]
  door_solenoid = female pin header, 2 pins [form="♀ (female)"]
  LED1 = smd LED [color="Red (633nm)" package="0603 [SMD]"]
  +12v_realy_power = female pin header, 1 pin [form="♀ (female)"]

nets:
  N1: U1.1, Pi_door_control_gpio.pin1
  N2: U1.2, R1.Pin_0
  N3: U1.3, +12v_realy_power.pin1
  N4: U1.4, 12_volt_relay.COIL1, LED1.cathode
  GND: 12_volt_relay.COIL2, R1.Pin_1, LED1.anode
  N5: 12_volt_relay.NO, door_solenoid.pin2
  N6: 12_volt_relay.MAIN, door_solenoid.pin1

notes:
  Door latch solenoid control.
  +3.3v on gpio buzzes open door.

custom parts:
  PS2502: LED-to-NPN high current optoisolator
